// Digital circuit Template.dig as structural Verilog
module Template (
  input  Cin,
  input  A,
  input  B,
  output Cout,
  output Sum
);

  wire not_1_out, not_2_out, not_3_out, or_1_out, or_2_out, or_3_out, or_4_out, or_5_out, or_6_out, or_7_out,
       or_8_out;

  not not_1 (not_1_out, A);
  not not_2 (not_2_out, B);
  not not_3 (not_3_out, Cin);
  or or_1 (or_1_out, A, B, Cin);
  or or_2 (or_2_out, A, B, not_3_out);
  or or_3 (or_3_out, A, not_2_out, Cin);
  or or_4 (or_4_out, not_1_out, B, Cin);
  or or_5 (or_5_out, A, B, Cin);
  or or_6 (or_6_out, A, not_2_out, not_3_out);
  or or_7 (or_7_out, B, not_3_out, not_1_out);
  or or_8 (or_8_out, Cin, not_2_out, not_1_out);
  and and_1 (Cout, or_1_out, or_2_out, or_3_out, or_4_out);
  and and_2 (Sum, or_5_out, or_6_out, or_7_out, or_8_out);
endmodule
