// Digital circuit Template.dig as structural Verilog
module Template (
  input  X0,
  input  X1,
  input  Selector,
  output Z
);

  wire and_1_out, and_2_out, ns, nx0, nx1;

  not not_1 (nx0, X0);
  not not_2 (nx1, X1);
  not not_3 (ns, Selector);
  and and_1 (and_1_out, X0, ns);
  and and_2 (and_2_out, X1, Selector);
  or or_1 (Z, and_1_out, and_2_out);

  // Other names for the same wires on the sheet: s = Selector
endmodule
