// Digital circuit Template.dig as structural Verilog
module Template (
  input  X1,
  input  Selector,
  input  X0,
  output Z
);

  wire ns, nx0, nx1, or_1_out, or_2_out;

  not not_1 (nx0, X0);
  not not_2 (nx1, X1);
  not not_3 (ns, Selector);
  or or_1 (or_1_out, X0, Selector);
  or or_2 (or_2_out, X1, ns);
  and and_1 (Z, or_1_out, or_2_out);

  // Other names for the same wires on the sheet: s = Selector
endmodule
