// Digital circuit Template.dig as structural Verilog
module Template (
  input  [3:0] ln,
  output a,
  output b,
  output c,
  output d,
  output e,
  output f,
  output g
);

  wire and_1_out, and_2_out, and_3_out, and_4_out, and_5_out, and_6_out, and_7_out, and_8_out, and_9_out,
       and_10_out, and_11_out, and_12_out, and_13_out, and_14_out, not_1_out, not_2_out, not_3_out;

  not not_1 (not_1_out, ln[2]);
  not not_2 (not_2_out, ln[1]);
  not not_3 (not_3_out, ln[0]);
  and and_1 (and_1_out, not_1_out, not_3_out);
  and and_2 (and_2_out, ln[2], ln[0]);
  and and_3 (and_3_out, not_2_out, not_3_out);
  and and_4 (and_4_out, ln[1], ln[0]);
  or or_1 (c, ln[2], not_2_out, ln[0]);
  and and_5 (and_5_out, not_1_out, not_3_out);
  and and_6 (and_6_out, not_1_out, ln[1]);
  and and_7 (and_7_out, ln[2], not_2_out, ln[0]);
  and and_8 (and_8_out, ln[1], not_3_out);
  and and_9 (and_9_out, not_1_out, not_3_out);
  and and_10 (and_10_out, ln[1], not_3_out);
  and and_11 (and_11_out, not_2_out, not_3_out);
  and and_12 (and_12_out, not_1_out, ln[1]);
  and and_13 (and_13_out, ln[2], not_2_out);
  and and_14 (and_14_out, ln[1], not_3_out);
  or or_2 (b, not_1_out, and_3_out, and_4_out);
  or or_3 (e, and_9_out, and_10_out);
  or or_4 (f, ln[3], ln[2], and_11_out);
  or or_5 (a, ln[3], and_1_out, and_2_out, ln[1]);
  or or_6 (d, ln[3], and_5_out, and_6_out, and_7_out, and_8_out);
  or or_7 (g, ln[3], and_12_out, and_13_out, and_14_out);
  Comparator comparator_1 ();  // open: a, b, gt, eq, lt
  Seven_Seg seven_seg_1 (.a(a), .b(b), .c(c), .d(d), .e(e), .f(f), .g(g), .dp(1'b0));
endmodule
