// Digital circuit Template.dig as structural Verilog
module Template (
  input  [2:0] In,
  input  clk,
  output [7:0] Z
);

  ROM #(.AddrBits(3), .Bits(8)) rom_1 (.A(In), .sel(1'b1), .D(Z));
  Terminal Digital (.D(Z), .C(clk), .en(1'b1));

  // Notes on the sheet:
  //   contents of rom_1 (hex, n*v repeats v):
  //   44,69,67,4c,6f,4c,61,62
endmodule
