// Digital circuit Templatet.dig as structural Verilog
module Templatet (
  input  [3:0] In,
  input  [1:0] Selector,
  output [3:0] Output
);

  ROM #(.AddrBits(6), .Bits(4)) rom_1 (.A({Selector, In}), .sel(1'b1), .D(Output));

  // Notes on the sheet:
  //   contents of rom_1 (hex, n*v repeats v):
  //   3,4,5,6,7,8,9,a,b,c,7*0,1,3,2,6,7,5,4,c,d,7*0,1,2,3,4,b,c,d,e
  //   ,f,7*0,5,2,9,4,b,6,d,a,f
endmodule
