// Digital circuit ErrorCorrectionCode.dig as structural Verilog
module ErrorCorrectionCode (
  input  [6:0] In,
  output [2:0] Out
);

  xor xor_1 (Out[2], In[3], In[2], In[1], In[0]);
  xor xor_2 (Out[1], In[5], In[4], In[1], In[0]);
  xor xor_3 (Out[0], In[6], In[4], In[2], In[0]);
  // Pins of 2 and 3 bits meet at Out
endmodule
