// Digital circuit Template.dig as structural Verilog
module Template (
  input  [6:0] In,
  output [6:0] Output
);

  wire [2:0] errorcorrectioncode_1_p2;
  wire [6:0] rom_1_d;

  // ErrorCorrectionCode errorcorrectioncode_1: pin names not known; wires that end beside it: In, errorcorrectioncode_1_p2
  ROM #(.AddrBits(3), .Bits(7)) rom_1 (.A(errorcorrectioncode_1_p2), .sel(1'b1), .D(rom_1_d));
  assign Output = rom_1_d ^ In;  // XOr xor_1, 7 bits wide

  // Notes on the sheet:
  //   contents of rom_1 (hex, n*v repeats v):
  //   0,40,20,10,8,4,2,1
endmodule
