// Digital circuit Template.dig as structural Verilog
module Template (
  input  [3:0] In,
  output [3:0] Output
);

  wire [2:0] neg_1_out, o;

  Neg #(.Bits(3)) neg_1 (.in(In[2:0]), .out(neg_1_out));
  Multiplexer #(.Bits(3)) multiplexer_1 (.sel(In[3]), .in_0(In[2:0]), .in_1(neg_1_out), .out(o));
  Multiplexer #(.Selector_Bits(3), .Bits(4)) multiplexer_2 (
    .sel(In[2:0]), .in_0(4'b0000), .in_1({In[3], o}), .in_2({In[3], o}), .in_3({In[3], o}),
    .in_4({In[3], o}), .in_5({In[3], o}), .in_6({In[3], o}), .in_7({In[3], o}), .out(Output));

  // Other names for the same wires on the sheet: o[3] = In[3]
endmodule
