// Digital circuit Template.dig as structural Verilog
module Template (
  input  [3:0] A,
  input  [3:0] B,
  input  [2:0] S,
  input  M,
  input  C,
  output [3:0] F
);

  wire [3:0] A_t, add_1_s, add_2_s, add_3_s, add_4_s, add_5_s, add_6_s, and_1_out, and_2_out, B_t,
       multiplexer_1_out, multiplexer_2_out, multiplexer_3_out, nand_1_out, neg_1_out, neg_2_out, neg_3_out,
       neg_4_out, neg_5_out, nor_1_out, or_1_out, xnor_1_out;
  wire [3:3] undriven;

  assign A_t = ~A;  // Not not_1, 4 bits wide
  assign B_t = ~B;  // Not not_2, 4 bits wide
  Neg #(.Bits(4)) neg_1 (.in(B), .out(neg_1_out));
  Add #(.Bits(4)) add_1 (.a(A), .b(neg_1_out), .c_i(1'b0), .s(add_1_s));  // open: c_o
  assign nand_1_out = ~(A & B);  // NAnd nand_1, 4 bits wide
  assign nor_1_out = ~(A | B);  // NOr nor_1, 4 bits wide
  assign xnor_1_out = ~(A ^ B);  // XNOr xnor_1, 4 bits wide
  assign and_1_out = A & B;  // And and_1, 4 bits wide
  assign or_1_out = A | B;  // Or or_1, 4 bits wide
  assign and_2_out = A & B_t;  // And and_2, 4 bits wide
  Neg #(.Bits(4)) neg_2 (.in({undriven[3], 3'b001}), .out(neg_2_out));
  Neg #(.Bits(4)) neg_3 (.in(4'b0001), .out(neg_3_out));
  Neg #(.Bits(4)) neg_4 (.in(A), .out(neg_4_out));
  Neg #(.Bits(4)) neg_5 (.in(4'b0001), .out(neg_5_out));
  Add #(.Bits(4)) add_2 (.a(A), .b(neg_2_out), .c_i(1'b0), .s(add_2_s));  // open: c_o
  Add #(.Bits(4)) add_3 (.a(A), .b(B), .c_i(1'b0), .s(add_3_s));  // open: c_o
  Add #(.Bits(4)) add_4 (.a(add_1_s), .b(neg_3_out), .c_i(1'b0), .s(add_4_s));  // open: c_o
  Add #(.Bits(4)) add_5 (.a(neg_4_out), .b(neg_5_out), .c_i(1'b0), .s(add_5_s));  // open: c_o
  Multiplexer #(.Selector_Bits(3), .Bits(4)) multiplexer_1 (
    .sel(S), .in_0(A_t), .in_1(nand_1_out), .in_2(nor_1_out), .in_3(xnor_1_out), .in_4(and_1_out),
    .in_5(or_1_out), .in_6(and_2_out), .in_7(A), .out(multiplexer_1_out));
  Multiplexer #(.Selector_Bits(3), .Bits(4)) multiplexer_2 (
    .sel(S), .in_0(A), .in_1(add_2_s), .in_2(add_3_s), .in_3(add_4_s), .in_4(add_5_s), .in_5(B),
    .in_6({A[2:0], 1'b0}), .in_7({1'b0, A[3:1]}), .out(multiplexer_2_out));
  Add #(.Bits(4)) add_6 (.a(multiplexer_2_out), .b(4'b0001), .c_i(1'b0), .s(add_6_s));  // open: c_o
  Multiplexer #(.Bits(4)) multiplexer_3 (.sel(C), .in_0(multiplexer_2_out), .in_1(add_6_s), .out(multiplexer_3_out));
  Multiplexer #(.Bits(4)) multiplexer_4 (.sel(M), .in_0(multiplexer_1_out), .in_1(multiplexer_3_out), .out(F));
  // Pins of 3 and 4 bits meet at {undriven[3], 3'b001}
endmodule
