// Digital circuit 01.dig as structural Verilog
module _01 (
  input  A0,
  input  A1,
  input  A2,
  input  B0,
  input  B1,
  input  B2
);

  wire add_1_c_o;
  wire [0:0] comparator_1_gt;
  wire [3:0] add_1_s;

  Add #(.Bits(4)) add_1 (.a({1'b0, A2, A1, A0}), .b({1'b0, B2, B1, B0}), .c_i(1'b0), .s(add_1_s), .c_o(add_1_c_o));
  Comparator #(.Bits(4)) comparator_1 (.a(add_1_s), .b(4'b1001), .gt(comparator_1_gt[0]));  // open: eq, lt
  Seven_Seg_Hex seven_seg_hex_1 (.d({3'b000, comparator_1_gt[0]}), .dp(1'b0));
  // also tied to GND on the sheet: add_1_c_o
endmodule
