// Digital circuit 02.dig as structural Verilog
module _02 (
  input  S0,
  input  S1,
  input  S2
);

  wire decoder_1_out_0, decoder_1_out_1, decoder_1_out_2, decoder_1_out_3, decoder_1_out_4, decoder_1_out_5,
       decoder_1_out_6, decoder_1_out_7, or_1_out, or_2_out;

  Decoder #(.Selector_Bits(3)) decoder_1 (
    .sel({S0, S1, S2}), .out_0(decoder_1_out_0), .out_1(decoder_1_out_1), .out_2(decoder_1_out_2),
    .out_3(decoder_1_out_3), .out_4(decoder_1_out_4), .out_5(decoder_1_out_5), .out_6(decoder_1_out_6),
    .out_7(decoder_1_out_7));
  // Probe on or_1_out
  or or_1 (or_1_out, decoder_1_out_6, decoder_1_out_5, decoder_1_out_4, decoder_1_out_2);
  // Probe on or_2_out
  or or_2 (or_2_out, decoder_1_out_7, decoder_1_out_6, decoder_1_out_4, decoder_1_out_2, decoder_1_out_0);
endmodule
